# Fritzing sketch teensy-snare (saved by Fritzing 0.9.9b)
circuit board: 2.19659cm x 5.5cm
breadboards: 1

parts:
  Teensy_LC = Teensy-LC
  100kΩ = Resistor [tolerance=±5% power=0.25 resistance=100k package=THT]
  100kΩ_2 = Resistor [tolerance=±5% power=0.25 resistance=100k package=THT]
  100kΩ_3 = Resistor [tolerance=±5% power=0.25 resistance=100k package=THT]
  Snare = Toggle Switch [package=THT]
  100kΩ_4 = Resistor [tolerance=±5% power=0.25 resistance=100k package=THT]

nets:
  N1: Teensy_LC.GND, 100kΩ_2.Pin_0, 100kΩ_3.Pin_0, Snare.L1
  N2: Teensy_LC.A0/D14, 100kΩ.Pin_1, 100kΩ_2.Pin_1
  N3: Teensy_LC.A1/D15, 100kΩ_3.Pin_1, 100kΩ_4.Pin_1
  N4: 100kΩ.Pin_0, Snare.COM
  N5: Snare.L2, 100kΩ_4.Pin_0

notes:
  snare
  isfopo
  1.0

custom parts:
  Teensy-LC: Teensy-LC (Low Cost) is a powerful 32 bit microcontroller board, with a rich set of hardware peripherals, at a very affordable price! Teensy-LC delivers an impressive collection of capabilities to make modern electronic projects simpler. It features an ARM Cortex-M0+ processor at 48 MHz, 62K Flash, 8K RAM, 12 bit analog input & output, hardware Serial, SPI & I2C, USB, and a total of 27 I/O pins.
